# Fritzing sketch PeristalticRelay (saved by Fritzing 0.9.3b)

parts:
  J7 = Camdenboss CTB0158-4 [part_number=CTB0158-4 package=THT]
  J8 = Camdenboss CTB0158-2 [part_number=CTB0158-2 package=THT]  # not connected
  J9 = Camdenboss CTB0158-2 [part_number=CTB0158-2 package=THT]  # not connected
  J10 = Camdenboss CTB0158-10 [part_number=CTB0158-10 package=THT]
  J11 = Camdenboss CTB0158-2 [part_number=CTB0158-2 package=THT]  # not connected
  J12 = Camdenboss CTB0158-2 [part_number=CTB0158-2 package=THT]  # not connected
  J13 = Camdenboss CTB0158-2 [part_number=CTB0158-2 package=THT]  # not connected
  J15 = Camdenboss CTB0158-6 [part_number=CTB0158-6 package=THT]
  J16 = Camdenboss CTB0158-2 [part_number=CTB0158-2 package=THT]  # not connected
  J17 = Camdenboss CTB0158-2 [part_number=CTB0158-2 package=THT]  # not connected
  J18 = Camdenboss CTB0158-2 [part_number=CTB0158-2 package=THT]  # not connected
  J19 = Camdenboss CTB0158-2 [part_number=CTB0158-2 package=THT]  # not connected
  J20 = Camdenboss CTB0158-2 [part_number=CTB0158-2 package=THT]  # not connected
  J21 = Camdenboss CTB0158-2 [part_number=CTB0158-2 package=THT]  # not connected
  J22 = Camdenboss CTB0158-2 [part_number=CTB0158-2 package=THT]
  J23 = Camdenboss CTB0158-10 [part_number=CTB0158-10 package=THT]
  J24 = Camdenboss CTB0158-10 [part_number=CTB0158-10 package=THT]
  SW2 = DIP Switch 8 Position [package=dipswitch-08]  # not connected
  SW3 = DIP Switch 8 Position [package=dipswitch-08]  # not connected
  J30 = Camdenboss CTB0158-2 [part_number=CTB0158-2 package=THT]
  J31 = Camdenboss CTB0158-2 [part_number=CTB0158-2 package=THT]  # not connected
  J32 = Camdenboss CTB0158-3 [part_number=CTB0158-3 package=THT]
  J33 = Camdenboss CTB0158-2 [part_number=CTB0158-2 package=THT]
  J34 = Camdenboss CTB0158-2 [part_number=CTB0158-2 package=THT]
  J35 = Camdenboss CTB0158-6 [part_number=CTB0158-6 package=THT]
  J36 = Camdenboss CTB0158-2 [part_number=CTB0158-2 package=THT]

nets:
  N1: J7.pin4, J35.pin1
  N2: J10.pin1, J23.pin8
  N3: J10.pin2, J23.pin7
  N4: J10.pin3, J23.pin6
  N5: J10.pin4, J23.pin5
  N6: J10.pin5, J23.pin4
  N7: J10.pin6, J23.pin3
  N8: J10.pin9, J23.pin2
  N9: J10.pin10, J23.pin1
  N10: J15.pin5, J35.pin3
  N11: J15.pin6, J35.pin2
  N12: J22.pin1, J24.terminal_10
  N13: J22.pin2, J24.terminal_9
  N14: J23.pin9, J24.pin9
  N15: J23.pin10, J24.pin10
  N16: J30.pin1, J32.pin1
  N17: J30.pin2, J32.pin2
  N18: J33.pin1, J34.pin2, J36.pin2
  N19: J33.pin2, J34.pin1, J36.pin1

notes:
  DE - D7
  RE - D4
  Q0.1 - D6
  Q0.0 - D5
  ARDBOX RELAY
  R4 - D9
  R5 - D10
  I0.9 - A5
  I0.8 - A4
  I0.7 - A3
  I0.6 - A2
  I0.5 - A1
  I0.4 - A0
  I0.3 - D1
  I0.2 - D0
  I0.1 - D3
  I0.0 - D2
  R6 - D11
  R7 - D12
  R8 - D13
  DO00
  DO01
  DO02
  DO03
  DO04
  DO05
  DO06
  DO07
  GND
  VCC
  DO13
  DO14
  DO09
  DO11
  DO08
  DO12
  DO15
  DO10
  MISO - D14
  MOSI - D13
  SCK - D15
  RESET
  5V
  B
  A
  RX - D1
  TX - D0
  SDA -D2
  SLC - D3
  R1 - D4
  R2 - D7
  R3 - D8
  24V
  12-24V
  ON= I0.0 / OFF = SDA
  ON= I0.1 / OFF = SLC
  ON= I0.2 / OFF = TX
  ON= I0.3 / OFF = RX
  ON= R1 / OFF = RE - D4
  ON= R2 / OFF = DE - D7
  ON= R6 / OFF = RO
  ON= RO / OFF = R6
  ON= R5 / OFF = DI
  ON= DI / OFF = R5
  12VDC
  Robot Logic Side
  Motor Power Side
  +
  -
  12V
  IN4
  IN3
  IN1
  ENB
  IN2
  ENA
  Warning! This is 0..10VDC
  Warning! Accepts 0..5VDC
  Can support 2 motors
  Avoid D0 and D1 which are for serial comms.
