# Fritzing sketch SyringeAnalog (saved by Fritzing 0.9.3b)

parts:
  J1 = Camdenboss CTB0158-2 [part_number=CTB0158-2 package=THT]
  J2 = Camdenboss CTB0158-2 [part_number=CTB0158-2 package=THT]
  J3 = Camdenboss CTB0158-4 [part_number=CTB0158-4 package=THT]
  J4 = Camdenboss CTB0158-2 [part_number=CTB0158-2 package=THT]
  J5 = Camdenboss CTB0158-2 [part_number=CTB0158-2 package=THT]
  J6 = Camdenboss CTB0158-2 [part_number=CTB0158-2 package=THT]  # not connected
  SW1 = DIP Switch 8 Position [package=dipswitch-08]  # not connected
  M2 = Stepper Motor - Bipolar
  J19 = Camdenboss CTB0158-2 [part_number=CTB0158-2 package=THT]  # not connected
  J22 = Camdenboss CTB0158-2 [part_number=CTB0158-2 package=THT]
  J23 = Camdenboss CTB0158-10 [part_number=CTB0158-10 package=THT]
  J24 = Camdenboss CTB0158-10 [part_number=CTB0158-10 package=THT]
  SW3 = DIP Switch 8 Position [package=dipswitch-08]  # not connected
  S5 = Pushbutton [package="[THT]"]
  S6 = Pushbutton [package="[THT]"]
  J20 = Camdenboss CTB0158-10 [part_number=CTB0158-10 package=THT]  # not connected
  J17 = Camdenboss CTB0158-7 [part_number=CTB0158-7 package=THT]  # not connected
  SW4 = DIP Switch 8 Position [package=dipswitch-08]  # not connected
  J16 = Camdenboss CTB0158-10 [part_number=CTB0158-10 package=THT]
  J25 = Camdenboss CTB0158-10 [part_number=CTB0158-10 package=THT]
  J9 = Camdenboss CTB0158-4 [part_number=CTB0158-4 package=THT]  # not connected
  SW7 = DIP Switch 8 Position [package=dipswitch-08]
  SW8 = DIP Switch 8 Position [package=dipswitch-08]

nets:
  N1: J1.pin1, J2.pin1
  N2: J1.pin2, J2.pin2
  N3: J3.pin1, M2.A
  N4: J3.pin2, M2.C
  N5: J3.pin3, M2.B
  N6: J3.pin4, M2.D
  N7: J4.pin1, J25.pin8
  N8: J4.pin2, J5.pin2, S5.Pin_3, S6.Pin_3, S6.Pin_4, J25.pin5
  N9: J5.pin1, J25.pin1
  N10: J22.pin1, J24.terminal_10
  N11: J22.pin2, J24.terminal_9
  N12: J23.pin1, J16.pin8
  N13: J23.pin2, J16.pin7
  N14: J23.pin3, J16.pin6
  N15: J23.pin4, J16.pin5
  N16: J23.pin5, J16.pin4
  N17: J23.pin6, J16.pin3
  N18: J23.pin7, J16.pin2
  N19: J23.pin8, J16.pin1
  N20: J23.pin9, J24.pin9
  N21: J23.pin10, J24.pin10
  N22: S5.Pin_2, J25.pin9
  N23: S6.Pin_2, J25.pin10
  N24: SW7.9, SW8.13
  N25: SW7.10, SW8.14
  N26: SW7.11, SW8.15
  N27: SW7.12, SW8.16

notes:
  +
  -
  VCC
  GND
  A+
  A-
  B+
  B-
  PUL+
  PUL-
  DIR+
  DIR-
  ENA+
  ENA-
  12VDC
  Q0.1 - D11
  Q0.0 - D13
  ARDBOX ANALOG
  I0.9 - A0
  I0.8 - A1
  I0.7 - A2
  I0.6 - A3
  I0.5 - A4
  I0.4 - A5
  I0.3 - D4
  I0.2 - D8
  I0.1 - D12
  I0.0 - D2
  DO00
  DO01
  DO02
  DO03
  DO04
  DO05
  DO06
  DO07
  DO13
  DO14
  DO09
  DO11
  DO08
  DO12
  DO15
  DO10
  MISO - D14
  MOSI - D13
  SCK - D15
  RESET
  5V
  Z-
  A0.0 - D13
  RX - D1
  TX - D0
  SDA -D2
  SLC - D3
  24V
  12-24V
  ON= I0.3 / OFF = RS#
  ON= RS# / OFF = I0.3
  ON= I0.2 / OFF = RS#
  ON= RS# / OFF = I0.2
  Negative Limit
  Positive Limit
  Motor Power Side
  Robot Logic Side
  Isolate from Motor Writes for Noise Suppresion
  24VCom
  GNDCom
  Q0.2 - D10
  Q0.3 - D9
  Q0.4 - D6
  Q0.5 - D5
  Q0.6 - D3
  Q0.7 - D12
  Q0.8 - D8
  Q0.9 - D4
  A0.1 - D11
  A0.2 - D10
  A0.3 - D9
  A0.4 - D6
  A0.5 - D5
  A0.6 - D3
  ON= Q0.0 / OFF = A0.0
  ON= Q0.1 / OFF = A0.1
  ON= Q0.2 / OFF = A0.2
  ON= Q0.3 / OFF = A0.3
  ON= Q0.4 / OFF = A0.4
  ON= Q0.5 / OFF = A0.5
  ON= Q0.6 / OFF = A0.6
  ON= HALF / OFF = FULL
  ON= DE / OFF = A0.2 | Q0.2
  ON= A0.2 | Q0.2 / OFF = DE
  ON= RE / OFF = A0.1 | Q0.1
  ON= A0.1 | Q0.1 / OFF = RE
  ON= I0.0 / OFF = SDA - D2
  ON= Q0.6 / OFF = SLC - D3
  Y+
