# Fritzing sketch SyringeRelay (saved by Fritzing 0.9.3b)

parts:
  J1 = Camdenboss CTB0158-2 [part_number=CTB0158-2 package=THT]
  J2 = Camdenboss CTB0158-2 [part_number=CTB0158-2 package=THT]
  J3 = Camdenboss CTB0158-4 [part_number=CTB0158-4 package=THT]
  J4 = Camdenboss CTB0158-2 [part_number=CTB0158-2 package=THT]
  J5 = Camdenboss CTB0158-2 [part_number=CTB0158-2 package=THT]
  J6 = Camdenboss CTB0158-2 [part_number=CTB0158-2 package=THT]  # not connected
  SW1 = DIP Switch 8 Position [package=dipswitch-08]  # not connected
  M2 = Stepper Motor - Bipolar
  J7 = Camdenboss CTB0158-4 [part_number=CTB0158-4 package=THT]
  J8 = Camdenboss CTB0158-2 [part_number=CTB0158-2 package=THT]  # not connected
  J9 = Camdenboss CTB0158-2 [part_number=CTB0158-2 package=THT]  # not connected
  J10 = Camdenboss CTB0158-10 [part_number=CTB0158-10 package=THT]
  J11 = Camdenboss CTB0158-2 [part_number=CTB0158-2 package=THT]  # not connected
  J12 = Camdenboss CTB0158-2 [part_number=CTB0158-2 package=THT]  # not connected
  J13 = Camdenboss CTB0158-2 [part_number=CTB0158-2 package=THT]  # not connected
  J15 = Camdenboss CTB0158-6 [part_number=CTB0158-6 package=THT]
  J16 = Camdenboss CTB0158-2 [part_number=CTB0158-2 package=THT]  # not connected
  J17 = Camdenboss CTB0158-2 [part_number=CTB0158-2 package=THT]  # not connected
  J18 = Camdenboss CTB0158-2 [part_number=CTB0158-2 package=THT]  # not connected
  J19 = Camdenboss CTB0158-2 [part_number=CTB0158-2 package=THT]  # not connected
  J20 = Camdenboss CTB0158-2 [part_number=CTB0158-2 package=THT]  # not connected
  J21 = Camdenboss CTB0158-2 [part_number=CTB0158-2 package=THT]  # not connected
  J22 = Camdenboss CTB0158-2 [part_number=CTB0158-2 package=THT]
  J23 = Camdenboss CTB0158-10 [part_number=CTB0158-10 package=THT]
  J24 = Camdenboss CTB0158-10 [part_number=CTB0158-10 package=THT]
  SW2 = DIP Switch 8 Position [package=dipswitch-08]  # not connected
  SW3 = DIP Switch 8 Position [package=dipswitch-08]  # not connected
  S5 = Pushbutton [package="[THT]"]
  S6 = Pushbutton [package="[THT]"]

nets:
  N1: J1.pin1, J2.pin1
  N2: J1.pin2, J2.pin2
  N3: J3.pin1, M2.A
  N4: J3.pin2, M2.C
  N5: J3.pin3, M2.B
  N6: J3.pin4, M2.D
  N7: J4.pin1, J15.pin4
  N8: J4.pin2, J5.pin2, J15.pin1, S5.Pin_3, S5.Pin_4, S6.Pin_3
  N9: J5.pin1, J7.pin1
  N10: J10.pin1, J23.pin8
  N11: J10.pin2, J23.pin7
  N12: J10.pin3, J23.pin6
  N13: J10.pin4, J23.pin5
  N14: J10.pin5, J23.pin4
  N15: J10.pin6, J23.pin3
  N16: J10.pin9, J23.pin2
  N17: J10.pin10, J23.pin1
  N18: J15.pin5, S5.Pin_2
  N19: J15.pin6, S6.Pin_2
  N20: J22.pin1, J24.terminal_10
  N21: J22.pin2, J24.terminal_9
  N22: J23.pin9, J24.pin9
  N23: J23.pin10, J24.pin10

notes:
  +
  -
  VCC
  GND
  A+
  A-
  B+
  B-
  PUL+
  PUL-
  DIR+
  DIR-
  ENA+
  ENA-
  12VDC
  DE - D7
  RE - D4
  Q0.1 - D6
  Q0.0 - D5
  ARDBOX RELAY
  R4 - D9
  R5 - D10
  I0.9 - A5
  I0.8 - A4
  I0.7 - A3
  I0.6 - A2
  I0.5 - A1
  I0.4 - A0
  I0.3 - D1
  I0.2 - D0
  I0.1 - D3
  I0.0 - D2
  R6 - D11
  R7 - D12
  R8 - D13
  DO00
  DO01
  DO02
  DO03
  DO04
  DO05
  DO06
  DO07
  DO13
  DO14
  DO09
  DO11
  DO08
  DO12
  DO15
  DO10
  MISO - D14
  MOSI - D13
  SCK - D15
  RESET
  5V
  B
  A
  RX - D1
  TX - D0
  SDA -D2
  SLC - D3
  R1 - D4
  R2 - D7
  R3 - D8
  24V
  12-24V
  ON= I0.0 / OFF = SDA
  ON= I0.1 / OFF = SLC
  ON= I0.2 / OFF = TX
  ON= I0.3 / OFF = RX
  ON= R1 / OFF = RE - D4
  ON= R2 / OFF = DE - D7
  ON= R6 / OFF = RO
  ON= RO / OFF = R6
  ON= R5 / OFF = DI
  ON= DI / OFF = R5
  Negative Limit
  Positive Limit
  Motor Power Side
  Robot Logic Side
  Isolate from Motor Writes for Noise Suppresion
